// Logisim project alu.circ as structural Verilog: 3 circuits, main circuit alu
module alu (
  input  [31:0] A,
  input  [31:0] B,
  input  [3:0] ALUSel,
  output [31:0] Result
);

  wire [31:0] add0, and0, mulHigh, mulHighU, mulLow, negator_1_out, or0, sll0, slt0, sra0, srl0, sub0, xor0;

  Adder #(.width(32)) adder_1 (.a(A), .b(B), .out(add0));  // open: cin, cout
  Comparator #(.width(32)) comparator_1 (.a(A), .b(B), .lt(slt0[0]));  // open: gt, eq
  assign xor0 = A ^ B;  // XOR_Gate xor_1, 32 bits wide
  assign or0 = A | B;  // OR_Gate or_1, 32 bits wide
  assign and0 = A & B;  // AND_Gate and_1, 32 bits wide
  Negator #(.width(32)) negator_1 (.in(B), .out(negator_1_out));
  Shifter #(.width(32)) shifter_1 (.in(A), .\dist (B[4:0]), .out(sll0));
  assign slt0[31:1] = {{30{1'b0}}, 1'b0};  // Bit_Extender bit_extender_1
  Shifter #(.shift("lr"), .width(32)) shifter_2 (.in(A), .\dist (B[4:0]), .out(srl0));
  Adder #(.width(32)) adder_2 (.a(A), .b(negator_1_out), .out(sub0));  // open: cin, cout
  Shifter #(.shift("ar"), .width(32)) shifter_3 (.in(A), .\dist (B[4:0]), .out(sra0));
  mul0 mul0_1 (.A(A), .B(B), .lowerBits(mulLow), .upperBits(mulHigh));
  mulhu0 mulhu0_1 (.A(A), .B(B), .upperUnsigned(mulHighU));
  Multiplexer #(.enable("false"), .select(4), .width(32)) multiplexer_1 (
    .in0(add0), .in1(sll0), .in2(slt0), .in4(xor0), .in5(srl0), .in6(or0), .in7(and0), .in8(mulLow),
    .in9(mulHigh), .in11(mulHighU), .in12(sub0), .in13(sra0), .in15(B), .out(Result), .sel(ALUSel));  // open: in3, in10, in14

  // Notes on the sheet:
  //   INPUTS to your circuit
  //   DON'T CHANGE THE LOCATIONS OF THE INPUTS AND OUTPUTS!
  //   OUTPUT from your circuit
endmodule

module mul0 (
  input  [31:0] A,
  input  [31:0] B,
  output [31:0] lowerBits,
  output [31:0] upperBits
);

  Multiplier #(.mode("twosComplement"), .width(32)) multiplier_1 (
    .a(A), .b(B), .out(lowerBits), .cout(upperBits));  // open: cin
endmodule

module mulhu0 (
  input  [31:0] A,
  input  [31:0] B,
  output [31:0] upperUnsigned
);

  Multiplier #(.width(32)) multiplier_1 (.a(A), .b(B), .cout(upperUnsigned));  // open: out, cin
endmodule
