// Logisim project branch-comp.circ as structural Verilog: 1 circuit, main circuit branch_comp
module branch_comp (
  input  [31:0] rs1,
  input  [31:0] rs2,
  input  BrUn,
  output BrEq,
  output BrLt
);

  wire [1:0] comparator_1_eq, comparator_2_eq;
  wire [31:0] demultiplexer_1_out0, demultiplexer_1_out1, demultiplexer_2_out0, demultiplexer_2_out1;

  Demultiplexer #(.enable("false"), .width(32)) demultiplexer_1 (
    .out0(demultiplexer_1_out0), .out1(demultiplexer_1_out1), .in(rs1), .sel(BrUn));
  Demultiplexer #(.enable("false"), .width(32)) demultiplexer_2 (
    .out0(demultiplexer_2_out0), .out1(demultiplexer_2_out1), .in(rs2), .sel(BrUn));
  Comparator #(.width(32)) comparator_1 (
    .a(demultiplexer_1_out0), .b(demultiplexer_2_out0), .eq(comparator_1_eq[0]), .lt(comparator_1_eq[1]));  // open: gt
  Comparator #(.mode("unsigned"), .width(32)) comparator_2 (
    .a(demultiplexer_1_out1), .b(demultiplexer_2_out1), .eq(comparator_2_eq[0]), .lt(comparator_2_eq[1]));  // open: gt
  Multiplexer #(.enable("false"), .width(2)) multiplexer_1 (
    .in0(comparator_1_eq), .in1(comparator_2_eq), .out({BrLt, BrEq}), .sel(BrUn));

  // Notes on the sheet:
  //   INPUTS to your circuit
  //   DON'T CHANGE THE LOCATIONS OF THE INPUTS AND OUTPUTS!
  //   OUTPUT from your circuit
endmodule
