// Logisim project control-logic.circ as structural Verilog: 14 circuits, main circuit control_logic
module control_logic (
  input  [31:0] inst,
  input  BrEq,
  input  BrLt,
  output PCSel,
  output out_5,
  output [2:0] ImmSel,
  output BrUn,
  output ASel,
  output BSel,
  output [3:0] ALUSel,
  output out_11,
  output [1:0] WBSel,
  output CSRSel,
  output CSRWen
);

  wire [31:0] I0, I1, I2, I3, R, S, SB, U0, U1, UJ;

  Demultiplexer #(.enable("false"), .select(5), .width(32)) demultiplexer_1 (
    .out0(I0), .out4(I1), .out5(U0), .out8(S), .out12(R), .out13(U1), .out24(SB), .out25(I2), .out27(UJ),
    .out28(I3), .in(inst), .sel(inst[6:2]));  // open: out1, out2, out3, out6, out7, out9, out10, out11, out14, out15, out16, out17, out18, out19, out20, out21, out22, out23, out26, out29, out30, out31
  alu_sel alu_sel_1 (.op(inst[6:0]), .funct7(inst[31:25]), .funct3(inst[14:12]), .sel(ALUSel));
  a_sel a_sel_1 (.op(inst[6:0]), .sel(ASel));
  b_sel b_sel_1 (.op(inst[6:0]), .sel(BSel));
  imm_sel imm_sel_1 (.op(inst[6:0]), .sel(ImmSel));
  wb_sel wb_sel_1 (.op(inst[6:0]), .sel(WBSel));
  pc_sel pc_sel_1 (.funct3(inst[14:12]), .BrEq(BrEq), .BrLt(BrLt), .op(inst[6:0]), .sel(PCSel));
  mem_sel mem_sel_1 (.op(inst[6:0]), .sel(out_11));
  reg_w_sel reg_w_sel_1 (.op(inst[6:0]), .sel(out_5));
  unsigned_branch_sel unsigned_branch_sel_1 (.funct3(inst[14:12]), .sel(BrUn));
  csr_wen csr_wen_1 (.op(inst[6:0]), .sel(CSRWen));

  // Other names for the same wires on the sheet: op[6:0] = inst[6:0]; funct3[2:0] = inst[14:12];
  //   funct7[6:0] = inst[31:25]; MemRw = out_11; RegWEn = out_5

  // Notes on the sheet:
  //   INPUTS to your circuit
  //   DeMUX for opcode
  //   Bits 0 and 1 are always 0b11 so they are excluded
  //   DON'T CHANGE THE LOCATIONS OF THE INPUTS AND OUTPUTS!
  //   OUTPUT from your circuit
endmodule

module r_alu (
  input  [6:0] funct7,
  input  [2:0] funct3,
  output [3:0] alu_sel
);

  wire and_1_out, and_2_out, and_3_out, and_4_out, and_5_out, and_6_out, and_7_out, and_8_out, and_9_out,
       and_10_out, and_11_out, and_12_out, and_13_out, and_14_out, not_1_out, not_2_out, not_3_out,
       not_4_out, not_5_out, not_6_out, not_7_out, not_8_out, not_9_out, not_10_out, not_11_out, not_12_out,
       not_13_out, not_14_out, not_15_out, not_16_out, not_17_out, not_18_out, not_19_out, not_20_out,
       not_21_out, not_22_out, not_23_out, not_24_out, not_25_out, not_26_out, not_27_out, not_28_out,
       not_29_out, not_30_out, not_31_out, not_32_out, not_33_out, not_34_out, not_35_out;

  not not_1 (not_1_out, funct7[0]);
  not not_2 (not_2_out, funct3[1]);
  not not_3 (not_3_out, funct7[0]);
  not not_4 (not_4_out, funct7[5]);
  not not_5 (not_5_out, funct7[5]);
  not not_6 (not_6_out, funct3[1]);
  not not_7 (not_7_out, funct3[2]);
  not not_8 (not_8_out, funct7[5]);
  not not_9 (not_9_out, funct3[2]);
  not not_10 (not_10_out, funct7[0]);
  not not_11 (not_11_out, funct3[1]);
  not not_12 (not_12_out, funct7[0]);
  not not_13 (not_13_out, funct7[5]);
  not not_14 (not_14_out, funct7[0]);
  not not_15 (not_15_out, funct3[0]);
  not not_16 (not_16_out, funct3[1]);
  not not_17 (not_17_out, funct3[2]);
  not not_18 (not_18_out, funct7[0]);
  not not_19 (not_19_out, funct3[1]);
  not not_20 (not_20_out, funct3[0]);
  not not_21 (not_21_out, funct3[1]);
  not not_22 (not_22_out, funct3[2]);
  not not_23 (not_23_out, funct7[5]);
  not not_24 (not_24_out, funct3[1]);
  not not_25 (not_25_out, funct3[2]);
  not not_26 (not_26_out, funct7[5]);
  not not_27 (not_27_out, funct3[2]);
  not not_28 (not_28_out, funct7[0]);
  not not_29 (not_29_out, funct7[5]);
  not not_30 (not_30_out, funct7[5]);
  not not_31 (not_31_out, funct3[2]);
  not not_32 (not_32_out, funct7[0]);
  not not_33 (not_33_out, funct7[5]);
  not not_34 (not_34_out, funct3[0]);
  not not_35 (not_35_out, funct7[0]);
  and and_1 (and_1_out, not_1_out, funct3[0], not_2_out, funct3[2]);
  and and_2 (and_2_out, not_3_out, not_4_out, funct3[0], funct3[2]);
  and and_3 (and_3_out, not_5_out, funct3[0], not_6_out, not_7_out);
  and and_4 (and_4_out, funct7[0], not_8_out, funct3[0], not_9_out);
  and and_5 (and_5_out, not_28_out, not_29_out, funct3[1], funct3[2]);
  and and_6 (and_6_out, funct7[0], not_30_out, funct3[0], funct3[1], not_31_out);
  and and_7 (and_7_out, not_32_out, not_33_out, not_34_out, funct3[1]);
  and and_8 (and_8_out, not_10_out, funct3[0], not_11_out, funct3[2]);
  and and_9 (and_9_out, not_12_out, not_13_out, funct3[2]);
  and and_10 (and_10_out, not_14_out, funct7[5], not_15_out, not_16_out, not_17_out);
  and and_11 (and_11_out, not_18_out, funct7[5], funct3[0], not_19_out, funct3[2]);
  and and_12 (and_12_out, not_35_out, funct7[5], not_20_out, not_21_out, not_22_out);
  and and_13 (and_13_out, funct7[0], not_23_out, not_24_out, not_25_out);
  and and_14 (and_14_out, funct7[0], not_26_out, funct3[0], not_27_out);
  or or_1 (alu_sel[0], and_1_out, and_2_out, and_3_out, and_4_out);
  or or_2 (alu_sel[1], and_5_out, and_6_out, and_7_out);
  or or_3 (alu_sel[2], and_8_out, and_9_out, and_10_out);
  or or_4 (alu_sel[3], and_11_out, and_12_out, and_13_out, and_14_out);

  // Other names for the same wires on the sheet: a0 = alu_sel[0]; a1 = alu_sel[1]; a2 = alu_sel[2]; a3 = alu_sel[3];
  //   c = funct3[0]; b = funct3[1]; a = funct3[2]; e = funct7[0]; d = funct7[5]

  // Notes on the sheet:
  //   ALU-SEl
endmodule

module i_alu (
  input  [6:0] funct7,
  input  [2:0] funct3,
  output [3:0] i_sel
);

  wire and_1_out, and_2_out, and_3_out, and_4_out, and_5_out, not_1_out, not_2_out, not_3_out;

  not not_1 (not_1_out, funct3[1]);
  not not_2 (not_2_out, funct3[0]);
  not not_3 (not_3_out, funct3[1]);
  and and_1 (and_1_out, funct3[0], funct3[2]);
  and and_2 (and_2_out, funct3[0], not_1_out);
  and and_3 (and_3_out, funct3[1], funct3[2]);
  and and_4 (and_4_out, not_2_out, funct3[1]);
  and and_5 (and_5_out, funct3[0], funct3[1]);
  and and_6 (i_sel[3], funct7[5], funct3[0], not_3_out, funct3[2]);
  or or_1 (i_sel[0], and_1_out, and_2_out);
  or or_2 (i_sel[1], and_3_out, and_4_out);
  or or_3 (i_sel[2], and_5_out, funct3[2]);

  // Other names for the same wires on the sheet: c = funct3[0]; b = funct3[1]; a = funct3[2]; e = funct7[0];
  //   d = funct7[5]; a0 = i_sel[0]; a1 = i_sel[1]; a2 = i_sel[2]; a3 = i_sel[3]
endmodule

module alu_sel (
  input  [6:0] op,
  input  [6:0] funct7,
  input  [2:0] funct3,
  output [3:0] sel
);

  wire is_i, is_lui, is_other, is_r, not_1_out, not_2_out, not_3_out, not_4_out, not_5_out, not_6_out,
       not_7_out, not_8_out, not_9_out, not_10_out, not_11_out, not_12_out;
  wire [1:0] priority_encoder_1_out;
  wire [3:0] i_sel, r_sel;

  not not_1 (not_1_out, op[3]);
  not not_2 (not_2_out, op[6]);
  not not_3 (not_3_out, op[2]);
  not not_4 (not_4_out, op[3]);
  not not_5 (not_5_out, op[6]);
  not not_6 (not_6_out, op[2]);
  not not_7 (not_7_out, op[3]);
  not not_8 (not_8_out, op[5]);
  not not_9 (not_9_out, op[6]);
  and and_1 (is_r, not_3_out, not_4_out, op[4], op[5], not_5_out);
  and and_2 (is_i, not_6_out, not_7_out, op[4], not_8_out, not_9_out);
  i_alu i_alu_1 (.funct7(funct7), .funct3(funct3), .i_sel(i_sel));
  and and_3 (is_lui, op[2], not_1_out, op[4], op[5], not_2_out);
  r_alu r_alu_1 (.funct7(funct7), .funct3(funct3), .alu_sel(r_sel));
  not not_10 (not_10_out, is_r);
  Priority_Encoder #(.select(2)) priority_encoder_1 (
    .in0(is_other), .in1(is_r), .in2(is_i), .in3(is_lui), .out(priority_encoder_1_out));  // open: gs, en_out, en_in
  not not_11 (not_11_out, is_lui);
  not not_12 (not_12_out, is_i);
  and and_4 (is_other, not_10_out, not_11_out, not_12_out);
  Multiplexer #(.enable("false"), .select(2), .width(4)) multiplexer_1 (
    .in0(4'b0000), .in1(r_sel), .in2(i_sel), .in3(4'b1111), .out(sel), .sel(priority_encoder_1_out));
endmodule

module a_sel (
  input  [6:0] op,
  output sel
);

  wire and_1_out, and_2_out, and_3_out, not_1_out, not_2_out, not_3_out, not_4_out, not_5_out, not_6_out,
       not_7_out;

  not not_1 (not_1_out, op[3]);
  not not_2 (not_2_out, op[5]);
  not not_3 (not_3_out, op[6]);
  not not_4 (not_4_out, op[4]);
  not not_5 (not_5_out, op[2]);
  not not_6 (not_6_out, op[3]);
  not not_7 (not_7_out, op[4]);
  and and_1 (and_1_out, op[2], not_1_out, op[4], not_2_out, not_3_out);
  and and_2 (and_2_out, op[2], op[3], not_4_out, op[5], op[6]);
  and and_3 (and_3_out, not_5_out, not_6_out, not_7_out, op[5], op[6]);
  or or_1 (sel, and_1_out, and_2_out, and_3_out);

  // Other names for the same wires on the sheet: e = op[2]; d = op[3]; c = op[4]; b = op[5]; a = op[6]
endmodule

module b_sel (
  input  [6:0] op,
  output sel
);

  wire not_1_out, not_2_out;

  not not_1 (not_1_out, op[4]);
  not not_2 (not_2_out, op[5]);
  or or_1 (sel, op[2], op[3], not_1_out, not_2_out, op[6]);

  // Other names for the same wires on the sheet: e = op[2]; d = op[3]; c = op[4]; b = op[5]; a = op[6]
endmodule

module imm_sel (
  input  [6:0] op,
  output [2:0] sel
);

  wire and_1_out, and_2_out, not_1_out, not_2_out, not_3_out, not_4_out, not_5_out, not_6_out, not_7_out,
       not_8_out, not_9_out;

  not not_1 (not_1_out, op[2]);
  not not_2 (not_2_out, op[3]);
  not not_3 (not_3_out, op[4]);
  not not_4 (not_4_out, op[3]);
  not not_5 (not_5_out, op[6]);
  not not_6 (not_6_out, op[2]);
  not not_7 (not_7_out, op[3]);
  not not_8 (not_8_out, op[4]);
  not not_9 (not_9_out, op[4]);
  and and_1 (and_1_out, not_1_out, not_2_out, not_3_out, op[5], op[6]);
  and and_2 (and_2_out, op[2], not_4_out, op[4], not_5_out);
  and and_3 (sel[1], not_6_out, not_7_out, not_8_out, op[5]);
  and and_4 (sel[2], op[2], op[3], not_9_out, op[5], op[6]);
  or or_1 (sel[0], and_1_out, and_2_out);

  // Other names for the same wires on the sheet: e = op[2]; d = op[3]; c = op[4]; b = op[5]; a = op[6]; i0 = sel[0];
  //   i1 = sel[1]; i2 = sel[2]
endmodule

module wb_sel (
  input  [6:0] op,
  output [1:0] sel
);

  wire and_1_out, and_2_out, and_3_out, and_4_out, not_1_out, not_2_out, not_3_out, not_4_out, not_5_out,
       not_6_out, not_7_out, not_8_out, not_9_out;

  not not_1 (not_1_out, op[5]);
  not not_2 (not_2_out, op[6]);
  not not_3 (not_3_out, op[2]);
  not not_4 (not_4_out, op[2]);
  and and_1 (and_1_out, not_1_out, op[6]);
  and and_2 (and_2_out, op[2], not_2_out);
  and and_3 (and_3_out, not_3_out, op[5]);
  and and_4 (and_4_out, not_4_out, op[3]);
  or or_1 (sel[0], and_1_out, and_2_out, and_3_out, op[4], and_4_out);
  not not_5 (not_5_out, op[2]);
  not not_6 (not_6_out, op[3]);
  not not_7 (not_7_out, op[4]);
  not not_8 (not_8_out, op[5]);
  not not_9 (not_9_out, op[6]);
  and and_5 (sel[1], not_5_out, not_6_out, not_7_out, not_8_out, not_9_out);

  // Other names for the same wires on the sheet: e = op[2]; d = op[3]; c = op[4]; b = op[5]; a = op[6]; w0 = sel[0];
  //   w1 = sel[1]
endmodule

module pc_sel (
  input  [2:0] funct3,
  input  BrEq,
  input  BrLt,
  input  [6:0] op,
  output sel
);

  wire branch_sel, is_branch, is_jump, multiplexer_1_out, not_1_out, not_2_out, not_3_out, not_4_out;

  not not_1 (not_1_out, op[4]);
  not not_2 (not_2_out, op[2]);
  not not_3 (not_3_out, op[3]);
  not not_4 (not_4_out, op[4]);
  and and_1 (is_jump, op[2], not_1_out, op[5], op[6]);
  and and_2 (is_branch, not_2_out, not_3_out, not_4_out, op[5], op[6]);
  Multiplexer #(.enable("false")) multiplexer_1 (.in0(1'b0), .in1(1'b1), .out(multiplexer_1_out), .sel(is_jump));
  Multiplexer #(.enable("false")) multiplexer_2 (.in0(multiplexer_1_out), .in1(branch_sel), .out(sel), .sel(is_branch));
  branch_pc branch_pc_1 (.funct3(funct3), .BrEq(BrEq), .BrLt(BrLt), .sel(branch_sel));

  // Other names for the same wires on the sheet: e = op[2]; d = op[3]; c = op[4]; b = op[5]; a = op[6]
endmodule

module branch_pc (
  input  [2:0] funct3,
  input  BrEq,
  input  BrLt,
  output sel
);

  wire and_1_out, and_2_out, and_3_out, and_4_out, and_5_out, not_1_out, not_2_out, not_3_out, not_4_out,
       not_5_out, not_6_out;

  not not_1 (not_1_out, BrLt);
  not not_2 (not_2_out, funct3[0]);
  not not_3 (not_3_out, BrEq);
  not not_4 (not_4_out, funct3[2]);
  not not_5 (not_5_out, funct3[0]);
  not not_6 (not_6_out, funct3[2]);
  and and_1 (and_1_out, BrEq, funct3[0], funct3[2]);
  and and_2 (and_2_out, not_1_out, funct3[0], funct3[2]);
  and and_3 (and_3_out, BrLt, not_2_out, funct3[2]);
  and and_4 (and_4_out, not_3_out, funct3[0], not_4_out);
  and and_5 (and_5_out, BrEq, not_5_out, not_6_out);
  or or_1 (sel, and_1_out, and_2_out, and_3_out, and_4_out, and_5_out);

  // Other names for the same wires on the sheet: f0 = funct3[0]; f1 = funct3[1]; f2 = funct3[2]; pc_Sel = sel
endmodule

module mem_sel (
  input  [6:0] op,
  output sel
);

  wire not_1_out, not_2_out, not_3_out, not_4_out;

  not not_1 (not_1_out, op[2]);
  not not_2 (not_2_out, op[3]);
  not not_3 (not_3_out, op[4]);
  not not_4 (not_4_out, op[6]);
  and and_1 (sel, not_1_out, not_2_out, not_3_out, op[5], not_4_out);

  // Other names for the same wires on the sheet: e = op[2]; d = op[3]; c = op[4]; b = op[5]; a = op[6]
endmodule

module reg_w_sel (
  input  [6:0] op,
  output sel
);

  wire not_1_out;

  not not_1 (not_1_out, op[5]);
  or or_1 (sel, op[2], op[3], op[4], not_1_out);

  // Other names for the same wires on the sheet: e = op[2]; d = op[3]; c = op[4]; b = op[5]; a = op[6]
endmodule

module unsigned_branch_sel (
  input  [2:0] funct3,
  output sel
);


  assign sel = funct3[1];
endmodule

module csr_wen (
  input  [6:0] op,
  output sel
);

  wire not_1_out, not_2_out;

  not not_1 (not_1_out, op[2]);
  not not_2 (not_2_out, op[3]);
  and and_1 (sel, not_1_out, not_2_out, op[4], op[5], op[6]);

  // Other names for the same wires on the sheet: e = op[2]; d = op[3]; c = op[4]; b = op[5]; a = op[6]
endmodule
