// Logisim project cpu.circ as structural Verilog: 1 circuit, main circuit cpu
module cpu (
  input  clk,
  input  [31:0] INSTRUCTION,
  input  [31:0] READ_DATA,
  output [31:0] WRITE_ADDRESS,
  output [31:0] PROGRAM_COUNTER,
  output [31:0] ra,
  output [31:0] sp,
  output [31:0] t0,
  output [31:0] t1,
  output [31:0] t2,
  output [31:0] s0,
  output [31:0] s1,
  output [31:0] a0,
  output [31:0] tohost,
  output [3:0] WRITE_ENABLE,
  output [31:0] WRITE_DATA
);

  wire a2, and_1_out, and_2_out, and_3_out, ASel, b2, BrEq, BrLt, BrUn, BSel, c2, CSRWen, d2, e2, f0, f1, f2,
       is_store, MemRW, not_1_out, not_2_out, not_3_out, not_4_out, not_5_out, not_6_out, not_7_out,
       not_8_out, not_9_out, not_10_out, or_1_out, PCSel, RegWEm, should_nop, undriven, undriven_2;
  wire [1:0] WBSel;
  wire [2:0] immSel;
  wire [3:0] ALUSel, byte_mask, half_mask, mem_mask;
  wire [4:0] bit_extender_2_out, bit_extender_3_out, bit_extender_4_out, bit_extender_5_out,
       multiplier_1_out, multiplier_2_out, multiplier_3_out, multiplier_4_out;
  wire [11:0] CSR_address;
  wire [19:0] INSTRUCTION2;
  wire [31:0] A, adder_1_out, adder_2_out, B, bit_extender_1_out, imm, load_byte_data, load_half_data,
       mem_data, multiplexer_1_out, multiplexer_2_out, multiplexer_3_out, multiplexer_4_out, PC2, read_data1,
       read_data2, shifter_5_out, shifter_6_out, store_byte_data, store_half_data, wb;

  Adder #(.width(32)) adder_1 (.a(PROGRAM_COUNTER), .b(32'h4), .out(adder_1_out));  // open: cin, cout
  Multiplexer #(.enable("false"), .width(32)) multiplexer_1 (
    .in0(adder_1_out), .in1(WRITE_ADDRESS), .out(multiplexer_1_out), .sel(PCSel));
  Register #(.width(32)) PC (.D(multiplexer_1_out), .en(1'b1), .clk(clk), .Q(PROGRAM_COUNTER), .clr(undriven));
  not not_1 (not_1_out, e2);
  not not_2 (not_2_out, d2);
  not not_3 (not_3_out, c2);
  not not_4 (not_4_out, c2);
  not not_5 (not_5_out, d2);
  not not_6 (not_6_out, c2);
  and and_1 (and_1_out, not_1_out, not_2_out, not_3_out, b2, a2);
  and and_2 (and_2_out, e2, d2, not_4_out, b2, a2);
  and and_3 (and_3_out, e2, not_5_out, not_6_out, b2, a2);
  Multiplexer #(.enable("false"), .width(32)) multiplexer_2 (
    .in0(INSTRUCTION), .in1(32'h13), .out(multiplexer_2_out), .sel(PCSel));
  Multiplexer #(.enable("false"), .width(32)) multiplexer_3 (
    .in0(PROGRAM_COUNTER), .out(multiplexer_3_out), .sel(1'b0));  // open: in1
  Register #(.width(32)) register_1 (
    .D(multiplexer_2_out), .en(1'b1), .clk(clk),
    .Q({CSR_address, INSTRUCTION2[19:15], f2, f1, f0, INSTRUCTION2[11:7], a2, b2, c2, d2, e2, INSTRUCTION2[1:0]}));  // open: clr
  Register #(.width(32)) register_2 (.D(multiplexer_3_out), .en(1'b1), .clk(clk), .Q(PC2), .clr(undriven_2));
  or or_1 (or_1_out, and_1_out, and_2_out, and_3_out);
  Register #(.width(1)) register_3 (.D(or_1_out), .en(1'b1), .clk(clk), .Q(should_nop));  // open: clr
  control_logic control_logic_1 (
    .CSRWen(CSRWen), .PCSel(PCSel), .out_5(RegWEm), .ImmSel(immSel), .BrUn(BrUn), .ASel(ASel), .BSel(BSel),
    .ALUSel(ALUSel), .out_11(MemRW), .WBSel(WBSel),
    .inst({CSR_address, INSTRUCTION2[19:15], f2, f1, f0, INSTRUCTION2[11:7], a2, b2, c2, d2, e2, INSTRUCTION2[1:0]}),
    .BrEq(BrEq), .BrLt(BrLt));  // open: CSRSel
  regfile regfile_1 (
    .rs1(INSTRUCTION2[19:15]), .rs2(CSR_address[4:0]), .rd(INSTRUCTION2[11:7]), .Write_Data(wb),
    .RegWEn(RegWEm), .clk(clk), .ra(ra), .sp(sp), .t0(t0), .t1(t1), .t2(t2), .s0(s0), .s1(s1), .a0(a0),
    .Read_Data_1(read_data1), .Read_Data_2(read_data2));
  imm_gen imm_gen_1 (
    .inst({CSR_address, INSTRUCTION2[19:15], f2, f1, f0, INSTRUCTION2[11:7], a2, b2, c2, d2, e2, INSTRUCTION2[1:0]}),
    .ImmSel(immSel), .imm(imm));
  assign bit_extender_1_out = {{27{1'b0}}, INSTRUCTION2[19:15]};  // Bit_Extender bit_extender_1
  Multiplexer #(.enable("false"), .width(32)) multiplexer_4 (
    .in0(read_data1), .in1(bit_extender_1_out), .out(multiplexer_4_out), .sel(f2));
  Multiplexer #(.enable("false"), .width(32)) multiplexer_5 (.in0(read_data1), .in1(PC2), .out(A), .sel(ASel));
  Multiplexer #(.enable("false"), .width(32)) multiplexer_6 (.in0(read_data2), .in1(imm), .out(B), .sel(BSel));
  branch_comp branch_comp_1 (.rs1(read_data1), .rs2(read_data2), .BrUn(BrUn), .BrEq(BrEq), .BrLt(BrLt));
  // csr csr_1: pin names not known; wires that end beside it: CSR_address, multiplexer_4_out, CSRWen, clk, tohost
  assign bit_extender_2_out = {{3{1'b0}}, WRITE_ADDRESS[1:0]};  // Bit_Extender bit_extender_2
  assign bit_extender_3_out = {{3{1'b0}}, WRITE_ADDRESS[1:0]};  // Bit_Extender bit_extender_3
  Multiplier #(.width(5)) multiplier_1 (
    .a(5'b01000), .b(bit_extender_2_out), .out(multiplier_1_out));  // open: cin, cout
  Multiplier #(.width(5)) multiplier_2 (
    .a(5'b01000), .b(bit_extender_3_out), .out(multiplier_2_out));  // open: cin, cout
  alu alu_1 (.Result(WRITE_ADDRESS), .A(A), .B(B), .ALUSel(ALUSel));
  not not_7 (not_7_out, e2);
  not not_8 (not_8_out, d2);
  not not_9 (not_9_out, c2);
  not not_10 (not_10_out, a2);
  Shifter #(.width(4)) shifter_1 (.in(4'b0001), .\dist (WRITE_ADDRESS[1:0]), .out(byte_mask));
  Shifter #(.width(4)) shifter_2 (.in(4'b0011), .\dist (WRITE_ADDRESS[1:0]), .out(half_mask));
  Multiplexer #(.enable("false"), .select(2), .width(4)) multiplexer_7 (
    .in0(byte_mask), .in1(half_mask), .in2(4'b1111), .out(mem_mask), .sel({f1, f0}));  // open: in3
  Shifter #(.width(32)) shifter_3 (.in(read_data2), .\dist (multiplier_1_out), .out(store_byte_data));
  Shifter #(.width(32)) shifter_4 (.in(read_data2), .\dist (multiplier_2_out), .out(store_half_data));
  Multiplexer #(.enable("false"), .select(2), .width(32)) multiplexer_8 (
    .in0(store_half_data), .in1(store_byte_data), .in2(read_data2), .out(WRITE_DATA), .sel({f1, f0}));  // open: in3
  Multiplexer #(.enable("false"), .width(4)) multiplexer_9 (
    .in0(4'b0000), .in1(mem_mask), .out(WRITE_ENABLE), .sel(MemRW));
  and and_4 (is_store, not_7_out, not_8_out, not_9_out, b2, not_10_out);
  assign bit_extender_4_out = {{3{1'b0}}, WRITE_ADDRESS[1:0]};  // Bit_Extender bit_extender_4
  Adder #(.width(32)) adder_2 (.a(PC2), .b(32'h4), .out(adder_2_out));  // open: cin, cout
  assign bit_extender_5_out = {{3{1'b0}}, WRITE_ADDRESS[1:0]};  // Bit_Extender bit_extender_5
  Multiplier #(.width(5)) multiplier_3 (
    .a(5'b01000), .b(bit_extender_4_out), .out(multiplier_3_out));  // open: cin, cout
  Multiplexer #(.enable("false"), .select(2), .width(32)) multiplexer_10 (
    .in0(load_byte_data), .in1(load_half_data), .in2(READ_DATA), .out(mem_data), .sel({f1, f0}));  // open: in3
  Multiplexer #(.enable("false"), .select(2), .width(32)) multiplexer_11 (
    .in0(adder_2_out), .in1(WRITE_ADDRESS), .in2(mem_data), .out(wb), .sel(WBSel));  // open: in3
  Multiplier #(.width(5)) multiplier_4 (
    .a(5'b01000), .b(bit_extender_5_out), .out(multiplier_4_out));  // open: cin, cout
  Shifter #(.shift("lr"), .width(32)) shifter_5 (.in(READ_DATA), .\dist (multiplier_3_out), .out(shifter_5_out));
  Shifter #(.shift("lr"), .width(32)) shifter_6 (.in(READ_DATA), .\dist (multiplier_4_out), .out(shifter_6_out));
  assign load_byte_data = {{24{shifter_6_out[7]}}, shifter_6_out[7:0]};  // Bit_Extender bit_extender_6
  assign load_half_data = {{16{shifter_5_out[15]}}, shifter_5_out[15:0]};  // Bit_Extender bit_extender_7

  // Other names for the same wires on the sheet: funct3_2[2:0] = {f2, f1, f0};
  //   INSTRUCTION2 (some bits) = {CSR_address, f2, f1, f0, a2, b2, c2, d2, e2};
  //   op2[6:0] = {a2, b2, c2, d2, e2, INSTRUCTION2[1:0]}; uimm[4:0] = INSTRUCTION2[19:15];
  //   funct7[6:0] = CSR_address[11:5]; offset_load[1:0] = WRITE_ADDRESS[1:0]; offset_store[1:0] = WRITE_ADDRESS[1:0];
  //   result[31:0] = WRITE_ADDRESS

  // Notes on the sheet:
  //   Output to IMEM
  //   Instruction Fetch
  //   IMEM (do **NOT** move this)
  //   Inputs from IMEM
  //   It is OK to move the PC, RegFile, ALU, MEM, Branch Comp, Imm Gen, and Control Logic to wherever is most convenient for you when constructing your CPU, and to delete this text
  //   Inputs/Outputs for testing. Do **NOT** move these.
  //   Execute
  //   Outputs To DMEM
  //   DMEM (do **NOT** move this)
  //   Inputs From DMEM
  //   Memory
  //   Write Back
endmodule
