// Logisim project regfile.circ as structural Verilog: 2 circuits, main circuit regfile
module regfile (
  input  [4:0] rs1,
  input  [4:0] rs2,
  input  [4:0] rd,
  input  [31:0] Write_Data,
  input  RegWEn,
  input  clk,
  output [31:0] ra,
  output [31:0] sp,
  output [31:0] t0,
  output [31:0] t1,
  output [31:0] t2,
  output [31:0] s0,
  output [31:0] s1,
  output [31:0] a0,
  output [31:0] Read_Data_1,
  output [31:0] Read_Data_2
);

  wire write_en1, write_en2, write_en3, write_en4, write_en5, write_en6, write_en7, write_en8, write_en9,
       write_en10, write_en11, write_en12, write_en13, write_en14, write_en15, write_en16, write_en17,
       write_en18, write_en19, write_en20, write_en21, write_en22, write_en23, write_en24, write_en25,
       write_en26, write_en27, write_en28, write_en29, write_en30, write_en31;
  wire [31:0] reg3, reg4, reg11, reg12, reg13, reg14, reg15, reg16, reg17, reg18, reg19, reg20, reg21, reg22,
       reg23, reg24, reg25, reg26, reg27, reg28, reg29, reg30, reg31;

  Demultiplexer #(.enable("false"), .select(5)) demultiplexer_1 (
    .out1(write_en1), .out2(write_en2), .out3(write_en3), .out4(write_en4), .out5(write_en5),
    .out6(write_en6), .out7(write_en7), .out8(write_en8), .out9(write_en9), .out10(write_en10),
    .out11(write_en11), .out12(write_en12), .out13(write_en13), .out14(write_en14), .out15(write_en15),
    .out16(write_en16), .out17(write_en17), .out18(write_en18), .out19(write_en19), .out20(write_en20),
    .out21(write_en21), .out22(write_en22), .out23(write_en23), .out24(write_en24), .out25(write_en25),
    .out26(write_en26), .out27(write_en27), .out28(write_en28), .out29(write_en29), .out30(write_en30),
    .out31(write_en31), .in(RegWEn), .sel(rd));  // open: out0
  Multiplexer #(.enable("false"), .select(5), .width(32)) multiplexer_1 (
    .in0({32{1'b0}}), .in1(ra), .in2(sp), .in3(reg3), .in4(reg4), .in5(t0), .in6(t1), .in7(t2), .in8(s0),
    .in9(s1), .in10(a0), .in11(reg11), .in12(reg12), .in13(reg13), .in14(reg14), .in15(reg15), .in16(reg16),
    .in17(reg17), .in18(reg18), .in19(reg19), .in20(reg20), .in21(reg21), .in22(reg22), .in23(reg23),
    .in24(reg24), .in25(reg25), .in26(reg26), .in27(reg27), .in28(reg28), .in29(reg29), .in30(reg30),
    .in31(reg31), .out(Read_Data_1), .sel(rs1));
  Multiplexer #(.enable("false"), .select(5), .width(32)) multiplexer_2 (
    .in0({32{1'b0}}), .in1(ra), .in2(sp), .in3(reg3), .in4(reg4), .in5(t0), .in6(t1), .in7(t2), .in8(s0),
    .in9(s1), .in10(a0), .in11(reg11), .in12(reg12), .in13(reg13), .in14(reg14), .in15(reg15), .in16(reg16),
    .in17(reg17), .in18(reg18), .in19(reg19), .in20(reg20), .in21(reg21), .in22(reg22), .in23(reg23),
    .in24(reg24), .in25(reg25), .in26(reg26), .in27(reg27), .in28(reg28), .in29(reg29), .in30(reg30),
    .in31(reg31), .out(Read_Data_2), .sel(rs2));
  regComponent regcomponent_1 (.write_data(Write_Data), .clk(clk), .write_en(write_en1), .reg_data(ra));
  regComponent regcomponent_2 (.write_data(Write_Data), .clk(clk), .write_en(write_en2), .reg_data(sp));
  regComponent regcomponent_3 (.write_data(Write_Data), .clk(clk), .write_en(write_en3), .reg_data(reg3));
  regComponent regcomponent_4 (.write_data(Write_Data), .clk(clk), .write_en(write_en4), .reg_data(reg4));
  regComponent regcomponent_5 (.write_data(Write_Data), .clk(clk), .write_en(write_en5), .reg_data(t0));
  regComponent regcomponent_6 (.write_data(Write_Data), .clk(clk), .write_en(write_en6), .reg_data(t1));
  regComponent regcomponent_7 (.write_data(Write_Data), .clk(clk), .write_en(write_en7), .reg_data(t2));
  regComponent regcomponent_8 (.write_data(Write_Data), .clk(clk), .write_en(write_en8), .reg_data(s0));
  regComponent regcomponent_9 (.write_data(Write_Data), .clk(clk), .write_en(write_en9), .reg_data(s1));
  regComponent regcomponent_10 (.write_data(Write_Data), .clk(clk), .write_en(write_en10), .reg_data(a0));
  regComponent regcomponent_11 (.write_data(Write_Data), .clk(clk), .write_en(write_en11), .reg_data(reg11));
  regComponent regcomponent_12 (.write_data(Write_Data), .clk(clk), .write_en(write_en12), .reg_data(reg12));
  regComponent regcomponent_13 (.write_data(Write_Data), .clk(clk), .write_en(write_en13), .reg_data(reg13));
  regComponent regcomponent_14 (.write_data(Write_Data), .clk(clk), .write_en(write_en14), .reg_data(reg14));
  regComponent regcomponent_15 (.write_data(Write_Data), .clk(clk), .write_en(write_en15), .reg_data(reg15));
  regComponent regcomponent_16 (.write_data(Write_Data), .clk(clk), .write_en(write_en16), .reg_data(reg16));
  regComponent regcomponent_17 (.write_data(Write_Data), .clk(clk), .write_en(write_en17), .reg_data(reg17));
  regComponent regcomponent_18 (.write_data(Write_Data), .clk(clk), .write_en(write_en18), .reg_data(reg18));
  regComponent regcomponent_19 (.write_data(Write_Data), .clk(clk), .write_en(write_en19), .reg_data(reg19));
  regComponent regcomponent_20 (.write_data(Write_Data), .clk(clk), .write_en(write_en20), .reg_data(reg20));
  regComponent regcomponent_21 (.write_data(Write_Data), .clk(clk), .write_en(write_en21), .reg_data(reg21));
  regComponent regcomponent_22 (.write_data(Write_Data), .clk(clk), .write_en(write_en22), .reg_data(reg22));
  regComponent regcomponent_23 (.write_data(Write_Data), .clk(clk), .write_en(write_en23), .reg_data(reg23));
  regComponent regcomponent_24 (.write_data(Write_Data), .clk(clk), .write_en(write_en24), .reg_data(reg24));
  regComponent regcomponent_25 (.write_data(Write_Data), .clk(clk), .write_en(write_en25), .reg_data(reg25));
  regComponent regcomponent_26 (.write_data(Write_Data), .clk(clk), .write_en(write_en26), .reg_data(reg26));
  regComponent regcomponent_27 (.write_data(Write_Data), .clk(clk), .write_en(write_en27), .reg_data(reg27));
  regComponent regcomponent_28 (.write_data(Write_Data), .clk(clk), .write_en(write_en28), .reg_data(reg28));
  regComponent regcomponent_29 (.write_data(Write_Data), .clk(clk), .write_en(write_en29), .reg_data(reg29));
  regComponent regcomponent_30 (.write_data(Write_Data), .clk(clk), .write_en(write_en30), .reg_data(reg30));
  regComponent regcomponent_31 (.write_data(Write_Data), .clk(clk), .write_en(write_en31), .reg_data(reg31));

  // Other names for the same wires on the sheet: read_data1[31:0] = Read_Data_1; read_data2[31:0] = Read_Data_2;
  //   read_reg1[4:0] = rs1; read_reg2[4:0] = rs2; reg1[31:0] = ra; reg2[31:0] = sp; reg5[31:0] = t0; reg6[31:0] = t1;
  //   reg7[31:0] = t2; reg8[31:0] = s0; reg9[31:0] = s1; reg10[31:0] = a0; write_en = RegWEn; write_reg[4:0] = rd

  // Notes on the sheet:
  //   INPUTS to your circuit
  //   DON'T CHANGE THE LOCATIONS OF THE INPUTS AND OUTPUTS!
  //   These are DEBUG/TEST outputs from your circuit.
  //   OUTPUTS from your circuit
endmodule

module regComponent (
  input  [31:0] write_data,
  input  clk,
  input  write_en,
  output [31:0] reg_data
);

  wire or_1_out;

  or or_1 (or_1_out, write_en, 1'b0);
  Register #(.width(32)) register_1 (.D(write_data), .en(or_1_out), .clk(clk), .Q(reg_data));  // open: clr
endmodule
