// Logisim project cpu-memory1.circ as structural Verilog: 1 circuit, main circuit run_main
module run_main (
  output [31:0] ra,
  output [31:0] sp,
  output [31:0] t0,
  output [31:0] t1,
  output [31:0] t2,
  output [31:0] s0,
  output [31:0] s1,
  output [31:0] a0,
  output [31:0] Requested_Address,
  output [31:0] Requested_Instruction,
  output [15:0] Time_Step,
  output halt
);

  wire clk;

  Clock clock_1 (.out(clk));
  // Probe on Requested_Address
  cpu_harness cpu_harness_1 (
    .INSTRUCTION(Requested_Instruction), .clk(clk), .PROGRAM_COUNTER(Requested_Address), .ra(ra), .sp(sp),
    .t0(t0), .t1(t1), .t2(t2), .s0(s0), .s1(s1), .a0(a0));
  ROM #(.addrWidth(14), .dataWidth(32)) rom_1 (.addr(Requested_Address[15:2]), .data(Requested_Instruction));
  // Probe on Requested_Instruction
  Counter #(.max('hffff), .width(16)) counter_1 (.clk(clk), .Q(Time_Step));  // open: clr, load, up, count, D, carry
  Comparator #(.width(16)) comparator_1 (.a(Time_Step), .b(16'h32), .eq(halt));  // open: gt, lt

  // Other names for the same wires on the sheet: INSTRUCTION[31:0] = Requested_Instruction;
  //   PROGRAM_COUNTER[31:0] = Requested_Address

  // Notes on the sheet:
  //   contents of rom_1 (hex, n*v repeats v):
  //   7D028293 60530313 628023 6280A3 628123 6281A3 FE628FA3 FE628E23 FE628F23 628523 FE628623 28303
  //   128303 228303 328303 528403 FFD28983 828903 FF928903 4B038393 1428313 63A023 3A303 1E30313 63A223
  //   43A303 2830313 638123 338303 1F30313 639123 239303 13030313 639023 39303 2930313 6390A3 139303
  //   5D30313 6380A3 238303 3A303 63A023 6381A3 43A303 639123 39303 338303
  //   Instruction Memory
  //   Halts Execution After Constant # of Clock Cycles
  //   Constant
endmodule
