// Logisim project cpu-registers.circ as structural Verilog: 1 circuit, main circuit run_main
module run_main (
  output [31:0] ra,
  output [31:0] sp,
  output [31:0] t0,
  output [31:0] t1,
  output [31:0] t2,
  output [31:0] s0,
  output [31:0] s1,
  output [31:0] a0,
  output [31:0] Requested_Address,
  output [31:0] Requested_Instruction,
  output [15:0] Time_Step,
  output halt
);

  wire clk;

  Clock clock_1 (.out(clk));
  // Probe on Requested_Address
  cpu_harness cpu_harness_1 (
    .INSTRUCTION(Requested_Instruction), .clk(clk), .PROGRAM_COUNTER(Requested_Address), .ra(ra), .sp(sp),
    .t0(t0), .t1(t1), .t2(t2), .s0(s0), .s1(s1), .a0(a0));
  ROM #(.addrWidth(14), .dataWidth(32)) rom_1 (.addr(Requested_Address[15:2]), .data(Requested_Instruction));
  // Probe on Requested_Instruction
  Counter #(.max('hffff), .width(16)) counter_1 (.clk(clk), .Q(Time_Step));  // open: clr, load, up, count, D, carry
  Comparator #(.width(16)) comparator_1 (.a(Time_Step), .b(16'h50), .eq(halt));  // open: gt, lt

  // Other names for the same wires on the sheet: INSTRUCTION[31:0] = Requested_Instruction;
  //   PROGRAM_COUNTER[31:0] = Requested_Address

  // Notes on the sheet:
  //   contents of rom_1 (hex, n*v repeats v):
  //   100013 1002B3 2002B3 3002B3 4002B3 FFE00093 200093 200113 FFE00113 300193 FFD00193 400213 FFC00213
  //   500293 600313 700393 800413 900493 A00513 B00593 C00613 D00693 E00713 F00793 1000813 1100893 1200913
  //   1300993 1400A13 1500A93 1600B13 1700B93 1800C13 1900C93 1A00D13 1B00D93 1C00E13 1D00E93 1E00F13
  //   1F00F93 FFC10113 112023 12083 410113 500293 600313 700393 800413 900493 A00513 B00593 C00613 D00693
  //   E00713 F00793 1000813 1100893 1200913 1300993 1400A13 1500A93 1600B13 1700B93 1800C13 1900C93
  //   1A00D13 1B00D93 1C00E13 1D00E93 1E00F13 1F00F93 FFE18193 FFD20213 218193 320213 FF908093 708093 8093
  //   Instruction Memory
  //   Halts Execution After Constant # of Clock Cycles
  //   Constant
endmodule
